# Fritzing sketch ControlBoardv2 (saved by Fritzing 0.9.3b)
perfboards: 1

parts:
  Fuse1 = Fuse with Handler [part_number=Htc-15m]
  D1 = Rectifier Diode [part_number=1N4001 package="300 mil [THT]"]
  J20 = male pin header, 4 pins [form="♂ (male)"]
  J22 = male pin header, 3 pins [form="♂ (male)"]
  J23 = male pin header, 2 pins [form="♂ (male)"]
  J24 = male pin header, 4 pins [form="♂ (male)"]
  J25 = male pin header, 5 pins [form="♂ (male)"]
  J26 = male pin header, 1 pin [form="♂ (male)"]
  J27 = male pin header, 2 pins [form="♂ (male)"]
  J29 = male pin header, 4 pins [form="♂ (male)"]
  J30 = male pin header, 4 pins [form="♂ (male)"]
  J31 = male pin header, 4 pins [form="♂ (male)"]
  J32 = male pin header, 4 pins [form="♂ (male)"]
  J33 = male pin header, 4 pins [form="♂ (male)"]
  J34 = male pin header, 4 pins [form="♂ (male)"]
  J35 = male pin header, 5 pins [form="♂ (male)"]
  J36 = male pin header, 6 pins [form="♂ (male)"]
  J21 = male pin header, 3 pins [form="♂ (male)"]
  J38 = male pin header, 3 pins [form="♂ (male)"]
  J37 = male pin header, 3 pins [form="♂ (male)"]
  J39 = male pin header, 8 pins [form="♂ (male)"]  # not connected
  J42 = Screw terminal - 2 pins [package=THT]
  J43 = male pin header, 4 pins [form="♂ (male)"]
  R1 = Resistor [tolerance=±5% resistance=220 package=THT]
  R2 = Resistor [tolerance=±5% resistance=220 package=THT]
  R3 = Resistor [tolerance=±5% resistance=220 package=THT]
  J46 = male pin header, 2 pins [form="♂ (male)"]
  J47 = male pin header, 3 pins [form="♂ (male)"]
  J28 = male pin header, 6 pins [form="♂ (male)"]
  J48 = male pin header, 4 pins [form="♂ (male)"]
  J49 = male pin header, 2 pins [form="♂ (male)"]

nets:
  N1: Fuse1.Connector1, D1.cathode
  N2: Fuse1.Connector2, J46.pin1
  N3: D1.anode, J42.pin1
  N4: J20.pin1, J46.pin2
  N5: J20.pin3, J35.pin5
  N6: J22.pin1, J36.pin4
  N7: J22.pin2, J36.pin3
  N8: J23.pin1, J29.pin2
  N9: J23.pin2, J29.pin3
  N10: J24.pin1, J33.pin2
  N11: J24.pin2, J33.pin3
  N12: J24.pin3, J30.pin2
  N13: J24.pin4, J30.pin3
  N14: J25.pin1, J31.pin1
  N15: J25.pin2, J32.pin2
  N16: J25.pin3, J32.pin3
  N17: J25.pin4, J31.pin2
  N18: J25.pin5, J31.pin3
  N19: J26.pin1, J34.pin4
  N20: J27.pin1, J34.pin1
  N21: J27.pin2, J34.pin2
  N22: J30.pin1, J32.pin1
  N23: J31.pin4, J42.pin2
  N24: J34.pin3, J49.pin1
  N25: J35.pin1, J48.pin4
  N26: J35.pin2, J48.pin3
  N27: J35.pin3, J48.pin2
  N28: J35.pin4, J48.pin1
  N29: J36.pin5, J21.pin1
  N30: J36.pin6, J21.pin2
  N31: J21.pin3, J37.pin1
  N32: J38.pin1, J28.pin1
  N33: J37.pin3, J28.pin2
  N34: J43.pin1, R3.Pin_0
  N35: J43.pin3, R2.Pin_0
  N36: R1.Pin_1, J47.pin3
  N37: R2.Pin_1, J47.pin2
  N38: R3.Pin_1, J47.pin1
  N39: J28.pin6, J49.pin2

notes:
  SPI
  Keyboard
  Display
  Power
  Accel / Gyro
  Led RGB
  Servo R
  Servo L
  Power Switch
  Top View
  Pin 2
  Buzzer
