# Fritzing sketch Sensor Board (Bottom Side) (saved by Fritzing 0.9.3b)
perfboards: 1

parts:
  IR_Front_Sensor_Connector_(Top) = female pin header, 2 pins [form="♀ (female)"]  # not connected
  IR_Front_Sensor_Connector_(Bottom) = female pin header, 2 pins [form="♀ (female)"]
  Part1 = Arduino Nano - Right pins
  Part2 = Arduino Nano - Left pins
  Part3 = SPI Connector
  Part4 = Arduino Nano - Left pins
  Part6 = APDS - 6 pins
  Part7 = APDS - 6 pins
  Part8 = QTR-8RC - Left 8 pins
  Part9 = QTR-8RC - Right 8 pins  # not connected
  Part10 = 74HC32 - Right pins  # not connected
  Part11 = 74HC32 - Left pins
  Part12 = Arduino Nano - Right pins

nets:
  N1: IR_Front_Sensor_Connector_(Bottom).pin2, Part12.A6
  VIN: Part1.VIN, Part3.VIN, Part12.VIN
  5V: Part1.5V, Part7.VCC
  N2: Part1.A4, Part7.SDA
  N3: Part2.D8, Part11.1A
  N4: Part2.D9, Part11.2B
  N5: Part3.SCK, Part12.D13
  N6: Part3.MISO, Part4.D12
  N7: Part3.MOSI, Part4.D11
  N8: Part3.SS, Part4.D10
  GND: Part3.GND, Part4.GND
  N9: Part4.D7, Part8.LEDON
  N10: Part6.SCL, Part11.1Y
  N11: Part7.SCL, Part11.2Y
  N12: Part11.1B, Part11.2A

notes:
  Bottom View
