# Fritzing sketch Sensor Board (Top Side) (saved by Fritzing 0.9.3b)
perfboards: 1

parts:
  Componente3 = Arduino Nano (Rev3.0)
  Componente4 = Arduino Nano (Rev3.0)
  J6 = female pin header, 2 pins [form="♀ (female)"]
  J7 = female pin header, 2 pins [form="♀ (female)"]  # not connected
  R20 = Resistor [tolerance=±5% resistance=220 package=THT]
  R21 = Resistor [tolerance=±5% resistance=1k package="0805 [SMD]"]  # not connected
  R22 = Resistor [tolerance=±5% resistance=1k package="0805 [SMD]"]  # not connected
  R23 = Resistor [tolerance=±5% resistance=100 package="0805 [SMD]"]
  R24 = Resistor [tolerance=±5% resistance=100 package="0805 [SMD]"]  # not connected
  Q11 = NPN-Transistor [package="TO92 [THT]"]
  Q12 = NPN-Transistor [package="TO92 [THT]"]
  R25 = Resistor [tolerance=±5% resistance=100 package=THT]  # not connected
  R26 = Resistor [tolerance=±5% resistance=100 package=THT]
  R27 = Resistor [tolerance=±5% resistance=47k package="0805 [SMD]"]  # not connected
  74HC33 = SN74LS32N [package="DIP14 [THT]"]  # not connected
  Part1 = QTR-8RC - Left 8 pins
  Part2 = QTR-8RC - Right 8 pins
  Part3 = SPI Connector  # not connected
  Part4 = APDS - 6 pins
  Part5 = APDS - 6 pins

nets:
  N1: Componente3.D2, Componente4.D0/RX
  N2: Componente3.D3, Componente4.D3
  N3: Componente3.D4, Componente4.D4
  N4: Componente3.D5, Componente4.D5
  N5: Componente3.D6, Componente4.D6
  N6: Componente4.A5, Part2.LED1
  N7: Componente4.A4, Part2.LED2
  N8: Componente4.A3, Part2.LED3
  N9: Componente4.A2, Part2.LED4
  N10: Componente4.A1, Part2.LED5
  N11: Componente4.A0, Part2.LED6
  N12: J6.pin2, R20.Pin_0
  N13: R23.Pin_0, Q12.E
  N14: R23.Pin_1, Part4.VCC
  N15: Q11.E, Part5.GND
  N16: Q11.C, R26.Pin_0
  GND1: Part1.GND1, Part1.GND2, Part1.GND3, Part1.GND4, Part1.GND5

notes:
  Top view
