# Fritzing sketch Sensor Board (saved by Fritzing 0.9.3b)
perfboards: 1

parts:
  Arduino_Nano_-_Line = Arduino Nano (Rev3.0)
  Arduino_Nano_-_Color = Arduino Nano (Rev3.0)
  R3 = Resistor [tolerance=±5% resistance=1k package="0805 [SMD]"]
  R4 = Resistor [tolerance=±5% resistance=1k package="0805 [SMD]"]
  R7 = Resistor [tolerance=±5% resistance=100 package="0805 [SMD]"]
  R8 = Resistor [tolerance=±5% resistance=100 package="0805 [SMD]"]
  R12 = Resistor [tolerance=±5% resistance=47k package="0805 [SMD]"]
  74HC32 = SN74LS32N [package="DIP14 [THT]"]
  IR_Front_Sensor_Connector_(Top) = female pin header, 2 pins [form="♀ (female)"]
  IR_Front_Sensor_Connector_(Bottom) = female pin header, 2 pins [form="♀ (female)"]
  Q9 = NPN-Transistor [package="TO92 [THT]"]
  Q10 = NPN-Transistor [package="TO92 [THT]"]
  R17 = Resistor [tolerance=±5% resistance=220 package=THT]
  R18 = Resistor [tolerance=±5% resistance=100 package=THT]
  R19 = Resistor [tolerance=±5% resistance=100 package=THT]  # not connected
  Part1 = SPI Connector
  Part2 = APDS - 6 pins
  Part3 = APDS - 6 pins
  Part4 = QTR-8RC - Left 8 pins
  Part5 = QTR-8RC - Right 8 pins

nets:
  N1: Arduino_Nano_-_Line.D0/RX, Arduino_Nano_-_Color.D2
  GND: Arduino_Nano_-_Line.GND, Part1.GND
  N2: Arduino_Nano_-_Line.D2, Part1.SS
  N3: Arduino_Nano_-_Line.D3, Arduino_Nano_-_Color.D3
  N4: Arduino_Nano_-_Line.D4, Arduino_Nano_-_Color.D4
  N5: Arduino_Nano_-_Line.D5, Arduino_Nano_-_Color.D5
  N6: Arduino_Nano_-_Line.D6, Arduino_Nano_-_Color.D6
  N7: Arduino_Nano_-_Line.D7, Part4.LEDON
  N8: Arduino_Nano_-_Line.D8, Part5.LED7
  N9: Arduino_Nano_-_Line.D9, Part5.LED8
  N10: Arduino_Nano_-_Line.D11/MOSI, Part1.MOSI
  N11: Arduino_Nano_-_Line.D12/MISO, Part1.MISO
  VIN: Arduino_Nano_-_Line.VIN, Arduino_Nano_-_Color.VIN, Part1.VIN
  N12: Arduino_Nano_-_Line.5V, R12.Pin_1
  N13: Arduino_Nano_-_Line.A6, R12.Pin_0, IR_Front_Sensor_Connector_(Bottom).pin1
  N14: Arduino_Nano_-_Line.A5, Part5.LED1
  N15: Arduino_Nano_-_Line.A4, Part5.LED2
  N16: Arduino_Nano_-_Line.A3, Part5.LED3
  N17: Arduino_Nano_-_Line.A2, Part5.LED4
  N18: Arduino_Nano_-_Line.A1, Part5.LED5
  N19: Arduino_Nano_-_Line.A0, Part5.LED6
  N20: Arduino_Nano_-_Line.D13/SCK, Part1.SCK
  N21: Arduino_Nano_-_Color.D8, 74HC32.1A
  N22: Arduino_Nano_-_Color.D9, 74HC32.2B
  N23: Arduino_Nano_-_Color.D12/MISO, R3.Pin_1
  5V: Arduino_Nano_-_Color.5V, R8.Pin_0, Part3.VCC
  N24: Arduino_Nano_-_Color.A4, Part3.SDA
  N25: Arduino_Nano_-_Color.D13/SCK, R4.Pin_1
  N26: R3.Pin_0, Q10.B
  N27: R4.Pin_0, Q9.B
  N28: R7.Pin_0, Q10.E
  N29: R7.Pin_1, Part2.VCC
  N30: 74HC32.1B, 74HC32.2A
  N31: 74HC32.1Y, Part2.SCL
  N32: 74HC32.2Y, Part3.SCL
  N33: 74HC32.GND, Q10.C
  N34: IR_Front_Sensor_Connector_(Top).pin2, R17.Pin_0
  N35: Q9.E, Part3.GND
  N36: Q9.C, R18.Pin_0
  GND_2: Part2.GND, Part4.GND1, Part4.GND2, Part4.GND3, Part4.GND4, Part4.GND5, Part4.GND6
